// Logisim project 4bit ALU.circ as structural Verilog: 9 circuits, main circuit main
// h.a
module main (
  input  in_1,
  input  in_2,
  output out_3,
  output out_4
);

  xor xor_1 (out_3, in_1, in_2);
  and and_1 (out_4, in_1, in_2);
endmodule

module DESIGN_AND_IMPLEMENTATION_OF_REGISTER_FILE (
  input  [7:0] in_1,
  input  in_2,
  input  in_3,
  input  in_4,
  output [7:0] out_5
);

  Register register_1 (.D(in_1), .en(in_2), .Q(out_5), .clk(in_3), .clr(in_4));
endmodule

module REGISTER_FILE (
  input  [1:0] RD_ADD_1,
  input  [1:0] WRITE_ADD,
  input  [1:0] RD_ADD_2,
  input  in_4,
  input  [3:0] in_5,
  input  CLK,
  input  REG_WR,
  output [3:0] READ_DATA_1,
  output [3:0] READ_DATA_2
);

  wire and_1_out, and_2_out, and_3_out, and_4_out, and_5_out, decoder_1_out0, decoder_1_out1, decoder_1_out2,
       decoder_1_out3, not_1_out, not_2_out;
  wire [3:0] register_1_q, register_2_q, register_3_q, register_4_q;

  Decoder #(.select(2), .enable("false")) decoder_1 (
    .out0(decoder_1_out0), .out1(decoder_1_out1), .out2(decoder_1_out2), .out3(decoder_1_out3),
    .sel(WRITE_ADD));
  and and_1 (and_1_out, not_1_out, CLK);
  not not_1 (not_1_out, REG_WR);
  and and_2 (and_2_out, decoder_1_out0, and_1_out);
  and and_3 (and_3_out, decoder_1_out1, and_1_out);
  and and_4 (and_4_out, decoder_1_out2, and_1_out);
  and and_5 (and_5_out, decoder_1_out3, and_1_out);
  Register #(.width(4), .trigger("falling")) register_1 (
    .D(in_5), .Q(register_1_q), .clk(and_2_out), .clr(not_2_out));  // open: en
  Register #(.width(4), .trigger("falling")) register_2 (
    .D(in_5), .Q(register_2_q), .clk(and_3_out), .clr(not_2_out));  // open: en
  Register #(.width(4), .trigger("falling")) register_3 (
    .D(in_5), .Q(register_3_q), .clk(and_4_out), .clr(not_2_out));  // open: en
  Register #(.width(4), .trigger("falling")) register_4 (
    .D(in_5), .Q(register_4_q), .clk(and_5_out), .clr(not_2_out));  // open: en
  not not_2 (not_2_out, in_4);
  Multiplexer #(.select(2), .width(4), .enable("false")) multiplexer_1 (
    .in0(register_1_q), .in1(register_2_q), .in2(register_3_q), .in3(register_4_q), .out(READ_DATA_1),
    .sel(RD_ADD_1));
  Multiplexer #(.select(2), .width(4), .enable("false")) multiplexer_2 (
    .in0(register_1_q), .in1(register_2_q), .in2(register_3_q), .in3(register_4_q), .out(READ_DATA_2),
    .sel(RD_ADD_2));

  // Notes on the sheet:
  //   WRITE DATA
  //   00
  //   10
  //   CLR
endmodule

module INSTRUCTION_MEMORY (
  input  [3:0] in_1,
  output [15:0] INSTRUCTIONS
);

  ROM #(.addrWidth(4), .dataWidth(16)) rom_1 (.addr(in_1), .data(INSTRUCTIONS));  // open: sel

  // Notes on the sheet:
  //   ADDRESS
  //   contents of rom_1 (hex, n*v repeats v):
  //   601 652 6a1 fc0 fd2 fe1 ec0 ed2 ee1 652 40a 318 fef
endmodule

module DATA_MEMORY (
  input  [3:0] in_1,
  input  CLK,
  input  [3:0] in_3,
  input  in_4,
  input  MWR,
  input  CLR,
  output [3:0] READ_DATA
);

  wire and_1_out, not_1_out, not_2_out, not_3_out, or_1_out;
  wire [3:0] ram_1_data;

  or or_1 (or_1_out, in_4, CLK);
  and and_1 (and_1_out, in_4, not_1_out);
  not not_1 (not_1_out, MWR);
  not not_2 (not_2_out, CLR);
  RAM #(.addrWidth(4), .dataWidth(4)) ram_1 (
    .addr(in_1), .data(ram_1_data), .clk(or_1_out), .ld(and_1_out), .clr(not_2_out));  // open: sel
  assign ram_1_data = not_3_out ? in_3 : 4'bz;  // Controlled_Buffer controlled_buffer_1
  not not_3 (not_3_out, and_1_out);
  assign READ_DATA = and_1_out ? ram_1_data : 4'bz;  // Controlled_Buffer controlled_buffer_2

  // Notes on the sheet:
  //   WRITE DATA
  //   ADDRESS
  //   MRD
  //   MRD= READ DATA
  //   MWR= WRITE DATA
endmodule

module PROGRAM_COUNTER (
  input  CLK,
  input  CLR,
  output [3:0] NEW_PC
);

  wire not_1_out;
  wire [3:0] adder_1_out;

  Register #(.width(4)) register_1 (.D(adder_1_out), .Q(NEW_PC), .clk(CLK), .clr(not_1_out));  // open: en
  not not_1 (not_1_out, CLR);
  Adder #(.width(4)) adder_1 (.a(4'b0001), .b(NEW_PC), .out(adder_1_out));  // open: cin, cout
endmodule

module CPU (
  input  in_1
);

  wire and_1_out, clock_1_out, n4_bit_a_l_u_1_zf, not_1_out, or_1_out;
  wire [1:0] multiplexer_1_out;
  wire [3:0] adder_1_out, adder_2_out, data_memory_1_read_data, multiplexer_2_out, multiplexer_3_out,
       multiplexer_4_out, multiplexer_5_out, n4_bit_a_l_u_1_result, register_1_q,
       register_file_1_read_data_1, register_file_1_read_data_2;
  wire [15:0] control_unit_1_out_2, instruction_memory_1_instructions;

  not not_1 (not_1_out, in_1);
  Clock clock_1 (.out(clock_1_out));
  Register #(.width(4)) register_1 (
    .D(multiplexer_4_out), .Q(register_1_q), .clk(clock_1_out), .clr(not_1_out));  // open: en
  INSTRUCTION_MEMORY instruction_memory_1 (.in_1(register_1_q), .INSTRUCTIONS(instruction_memory_1_instructions));
  Adder #(.width(4)) adder_1 (.a(register_1_q), .b(4'b0001), .out(adder_1_out));  // open: cin, cout
  Multiplexer #(.width(2), .enable("false")) multiplexer_1 (
    .in0(instruction_memory_1_instructions[5:4]), .in1(instruction_memory_1_instructions[3:2]),
    .out(multiplexer_1_out), .sel(control_unit_1_out_2[4]));
  or or_1 (or_1_out, clock_1_out, control_unit_1_out_2[7]);
  CONTROL_UNIT control_unit_1 (.in_1(instruction_memory_1_instructions[11:8]), .out_2(control_unit_1_out_2));
  REGISTER_FILE register_file_1 (
    .in_5(multiplexer_5_out), .READ_DATA_1(register_file_1_read_data_1),
    .RD_ADD_1(instruction_memory_1_instructions[7:6]), .READ_DATA_2(register_file_1_read_data_2),
    .RD_ADD_2(instruction_memory_1_instructions[5:4]), .REG_WR(or_1_out), .CLK(clock_1_out), .in_4(in_1),
    .WRITE_ADD(multiplexer_1_out));
  Adder #(.width(4)) adder_2 (
    .a(adder_1_out), .b(instruction_memory_1_instructions[3:0]), .out(adder_2_out));  // open: cin, cout
  Multiplexer #(.width(4), .enable("false")) multiplexer_2 (
    .in0(register_file_1_read_data_2), .in1(instruction_memory_1_instructions[3:0]), .out(multiplexer_2_out),
    .sel(control_unit_1_out_2[2]));
  and and_1 (and_1_out, control_unit_1_out_2[1], n4_bit_a_l_u_1_zf);
  Multiplexer #(.width(4), .enable("false")) multiplexer_3 (
    .in0(adder_1_out), .in1(adder_2_out), .out(multiplexer_3_out), .sel(and_1_out));
  _4__BIT_A_L__U u_4_bit_a_l_u_1 (
    .A(register_file_1_read_data_1), .B(multiplexer_2_out), .Result(n4_bit_a_l_u_1_result),
    .ZF(n4_bit_a_l_u_1_zf), .BIN(control_unit_1_out_2[9]), .CIN(control_unit_1_out_2[8]),
    .OP(control_unit_1_out_2[11:10]));  // open: SF, OF, CF
  Multiplexer #(.width(4), .enable("false")) multiplexer_4 (
    .in0(instruction_memory_1_instructions[3:0]), .in1(multiplexer_3_out), .out(multiplexer_4_out),
    .sel(control_unit_1_out_2[0]));
  DATA_MEMORY data_memory_1 (
    .in_1(n4_bit_a_l_u_1_result), .CLK(clock_1_out), .in_3(register_file_1_read_data_2),
    .READ_DATA(data_memory_1_read_data), .in_4(control_unit_1_out_2[5]), .MWR(control_unit_1_out_2[6]),
    .CLR(in_1));
  Multiplexer #(.width(4), .enable("false")) multiplexer_5 (
    .in0(data_memory_1_read_data), .in1(n4_bit_a_l_u_1_result), .out(multiplexer_5_out),
    .sel(control_unit_1_out_2[3]));

  // Notes on the sheet:
  //   rgdst
  //   SW
  //   alu src
  //   branch
  //   jump
  //   mtor
  //   LW
endmodule

module _4__BIT_A_L__U (
  input  CIN,
  input  BIN,
  input  [1:0] OP,
  input  [3:0] A,
  input  [3:0] B,
  output [3:0] Result,
  output ZF,
  output SF,
  output OF,
  output CF
);

  wire n1_bit_alu_1_p7, n1_bit_alu_2_p7, n1_bit_alu_3_p7;

  // _1_bit_alu 1_bit_alu_1: pin names not known; wires that end beside it: A[0], B[0], BIN, CIN, OP, Result[0], n1_bit_alu_1_p7
  // _1_bit_alu 1_bit_alu_2: pin names not known; wires that end beside it: A[1], B[1], BIN, n1_bit_alu_1_p7, OP, Result[1], n1_bit_alu_2_p7
  // _1_bit_alu 1_bit_alu_3: pin names not known; wires that end beside it: A[2], B[2], BIN, n1_bit_alu_2_p7, OP, Result[2], n1_bit_alu_3_p7
  // _1_bit_alu 1_bit_alu_4: pin names not known; wires that end beside it: A[3], B[3], BIN, n1_bit_alu_3_p7, OP, Result[3], CF
  nor nor_1 (ZF, Result[0], Result[1], Result[2], Result[3]);
  xor xor_1 (OF, n1_bit_alu_3_p7, CF);

  assign SF = Result[3];

  // Notes on the sheet:
  //   4 bit ALU
  //   LSB
  //   MSB
endmodule

module CONTROL_UNIT (
  input  [3:0] in_1,
  output [15:0] out_2
);

  ROM #(.addrWidth(4), .dataWidth(16)) rom_1 (.addr(in_1), .data(out_2));  // open: sel

  // Notes on the sheet:
  //   contents of rom_1 (hex, n*v repeats v):
  //   79 479 879 b79 6d 46d 86d b6d f79 f6d b83 b83 80 1 825 8cd
endmodule
