// Logisim project COAL project.circ as structural Verilog: 19 circuits, main circuit main
module main (
  input  in_1,
  input  in_2,
  input  [3:0] in_3,
  input  [3:0] in_4,
  input  [1:0] in_5,
  input  [3:0] in_6,
  input  in_7,
  input  in_8,
  input  in_9,
  input  in_10,
  input  [3:0] in_11,
  output [3:0] out_12,
  output [3:0] out_13
);

  Program_counter program_counter_1 (
    .in_1(in_6), .clock(in_7), .clr(in_8), .out_7(out_13), .offset(in_11), .brn(in_10), .jmp(in_9));
  _4_bit_ALU u_4_bit_alu_1 (
    .C_in(in_2), .in_2(in_5), .A(in_3), .B_inv(in_1), .B(in_4), .out_6(out_12));  // open: ZF, OF, SF, CF
endmodule

module HALF_ADDER (
  input  A,
  input  B,
  output SUM,
  output CARRY
);

  xor xor_1 (SUM, A, B);
  and and_1 (CARRY, A, B);
endmodule

module FULL_ADDER (
  input  C_IN,
  input  A,
  input  B,
  output SUM,
  output C_OUT
);

  wire and_1_out, half_adder_1_carry, half_adder_1_sum;

  HALF_ADDER half_adder_1 (.A(A), .B(B), .SUM(half_adder_1_sum), .CARRY(half_adder_1_carry));
  and and_1 (and_1_out, half_adder_1_sum, C_IN);
  xor xor_1 (SUM, half_adder_1_sum, C_IN);
  or or_1 (C_OUT, and_1_out, half_adder_1_carry);
endmodule

module ADDER_SUBTRACTOR (
  input  C_IN,
  input  A,
  input  B,
  input  Binv,
  output out_5,
  output C_OUT
);

  wire multiplexer_1_out, not_1_out;

  Multiplexer #(.enable("false")) multiplexer_1 (.in0(B), .in1(not_1_out), .out(multiplexer_1_out), .sel(Binv));
  not not_1 (not_1_out, B);
  FULL_ADDER full_adder_1 (.C_IN(C_IN), .A(A), .B(multiplexer_1_out), .SUM(out_5), .C_OUT(C_OUT));

  // Notes on the sheet:
  //                     SUM/SUB
endmodule

module _4_bit_adder_subtractor (
  input  C_IN,
  input  B_INV,
  input  [3:0] A,
  input  [3:0] B,
  output [3:0] out_5,
  output C_OUT
);

  wire adder_subtractor_1_c_out, adder_subtractor_2_c_out, adder_subtractor_3_c_out;

  ADDER_SUBTRACTOR adder_subtractor_1 (
    .C_IN(C_IN), .A(A[0]), .B(B[0]), .Binv(B_INV), .out_5(out_5[0]), .C_OUT(adder_subtractor_1_c_out));
  ADDER_SUBTRACTOR adder_subtractor_2 (
    .C_IN(adder_subtractor_1_c_out), .A(A[1]), .B(B[1]), .Binv(B_INV), .out_5(out_5[1]),
    .C_OUT(adder_subtractor_2_c_out));
  ADDER_SUBTRACTOR adder_subtractor_3 (
    .C_IN(adder_subtractor_2_c_out), .A(A[2]), .B(B[2]), .Binv(B_INV), .out_5(out_5[2]),
    .C_OUT(adder_subtractor_3_c_out));
  ADDER_SUBTRACTOR adder_subtractor_4 (
    .C_IN(adder_subtractor_3_c_out), .A(A[3]), .B(B[3]), .Binv(B_INV), .out_5(out_5[3]), .C_OUT(C_OUT));
endmodule

module _4_bit_ALU (
  input  C_in,
  input  [1:0] in_2,
  input  [3:0] A,
  input  B_inv,
  input  [3:0] B,
  output [3:0] out_6,
  output ZF,
  output OF,
  output SF,
  output CF
);

  wire n1_bit_alu_1_c_out, n1_bit_alu_2_c_out, n1_bit_alu_3_c_out, n1_bit_alu_4_set;

  _1_bit_ALU u_1_bit_alu_1 (
    .C_IN(C_in), .A(A[0]), .B(B[0]), .Binv(B_inv), .in_5(in_2), .OUTPUT(out_6[0]),
    .C_OUT(n1_bit_alu_1_c_out), .less(n1_bit_alu_4_set));  // open: set
  _1_bit_ALU u_1_bit_alu_2 (
    .C_IN(n1_bit_alu_1_c_out), .A(A[1]), .B(B[1]), .Binv(B_inv), .in_5(in_2), .OUTPUT(out_6[1]),
    .C_OUT(n1_bit_alu_2_c_out), .less(1'b0));  // open: set
  _1_bit_ALU u_1_bit_alu_3 (
    .C_IN(n1_bit_alu_2_c_out), .A(A[2]), .B(B[2]), .Binv(B_inv), .in_5(in_2), .OUTPUT(out_6[2]),
    .C_OUT(n1_bit_alu_3_c_out), .less(1'b0));  // open: set
  _1_bit_ALU u_1_bit_alu_4 (
    .C_IN(n1_bit_alu_3_c_out), .A(A[3]), .B(B[3]), .Binv(B_inv), .in_5(in_2), .OUTPUT(out_6[3]), .C_OUT(CF),
    .less(1'b0), .set(n1_bit_alu_4_set));
  xor xor_1 (OF, n1_bit_alu_3_c_out, CF);
  nor nor_1 (ZF, out_6[0], out_6[1], out_6[2], out_6[3]);

  assign SF = out_6[3];

  // Notes on the sheet:
  //   S0
  //   S1
  //   S2
  //   S3
endmodule

module _1_bit_ALU (
  input  C_IN,
  input  A,
  input  B,
  input  Binv,
  input  [1:0] in_5,
  input  less,
  output OUTPUT,
  output C_OUT,
  output set
);

  wire and_1_out, or_1_out;

  and and_1 (and_1_out, A, B);
  or or_1 (or_1_out, A, B);
  ADDER_SUBTRACTOR adder_subtractor_1 (.C_IN(C_IN), .A(A), .B(B), .Binv(Binv), .out_5(set), .C_OUT(C_OUT));
  Multiplexer #(.select(2), .enable("false")) multiplexer_1 (
    .in0(and_1_out), .in1(or_1_out), .in2(set), .in3(less), .out(OUTPUT), .sel(in_5));
endmodule

module _4_bit_adder (
  input  in_1,
  input  [3:0] A,
  input  [3:0] B,
  output [3:0] SUM,
  output out_5
);

  wire full_adder_1_c_out, full_adder_2_c_out, full_adder_3_c_out;

  FULL_ADDER full_adder_1 (.C_IN(in_1), .A(A[0]), .B(B[0]), .SUM(SUM[0]), .C_OUT(full_adder_1_c_out));
  FULL_ADDER full_adder_2 (.C_IN(full_adder_1_c_out), .A(A[1]), .B(B[1]), .SUM(SUM[1]), .C_OUT(full_adder_2_c_out));
  FULL_ADDER full_adder_3 (.C_IN(full_adder_2_c_out), .A(A[2]), .B(B[2]), .SUM(SUM[2]), .C_OUT(full_adder_3_c_out));
  FULL_ADDER full_adder_4 (.C_IN(full_adder_3_c_out), .A(A[3]), .B(B[3]), .SUM(SUM[3]), .C_OUT(out_5));
endmodule

module _8_bit_adder (
  input  in_1,
  input  [7:0] in_2,
  input  [7:0] B,
  output [7:0] out_4,
  output out_5
);

  wire n4_bit_adder_1_out_5;

  _4_bit_adder u_4_bit_adder_1 (.out_5(n4_bit_adder_1_out_5), .SUM(out_4[3:0]), .in_1(in_1), .A(in_2[3:0]), .B(B[3:0]));
  _4_bit_adder u_4_bit_adder_2 (
    .out_5(out_5), .SUM(out_4[7:4]), .in_1(n4_bit_adder_1_out_5), .A(in_2[7:4]), .B(B[7:4]));

  // Notes on the sheet:
  //   A
endmodule

module RAM1 (
  input  [3:0] in_1,
  input  [2:0] in_2,
  input  CLK,
  input  in_4,
  input  in_5,
  output [3:0] out_6
);

  wire not_1_out;

  assign out_6 = in_5 ? in_1 : 4'bz;  // Controlled_Buffer controlled_buffer_1
  not not_1 (not_1_out, in_5);
  RAM #(.addrWidth(3), .dataWidth(4)) ram_1 (
    .addr(in_2), .data(out_6), .sel(CLK), .clk(in_4), .ld(not_1_out));  // open: clr
endmodule

module TASK (
  input  [2:0] STARTING,
  input  INCREMENT,
  input  in_3,
  input  in_4,
  input  CLK,
  input  in_6,
  input  RESET,
  input  in_8,
  input  in_9,
  output [2:0] PC,
  output [3:0] out_11
);

  wire [3:0] multiplexer_1_out, n4_bit_adder_1_sum, rom_1_data;

  Counter #(.width(3), .max('h7)) counter_1 (
    .D(STARTING), .count(INCREMENT), .Q(PC), .clk(CLK), .clr(RESET));  // open: load, carry
  ROM #(.addrWidth(3), .dataWidth(4)) rom_1 (.addr(PC), .data(rom_1_data), .sel(in_6));
  Multiplexer #(.width(4), .enable("false")) multiplexer_1 (
    .in0(rom_1_data), .in1(n4_bit_adder_1_sum), .out(multiplexer_1_out), .sel(in_3));
  RAM #(.addrWidth(3), .dataWidth(4), .bus("separate")) ram_1 (
    .addr(PC), .din(multiplexer_1_out), .data(out_11), .str(in_4), .sel(in_8), .clk(CLK), .clr(in_9));  // open: ld
  _4_bit_adder u_4_bit_adder_1 (.SUM(n4_bit_adder_1_sum), .in_1(1'b0), .A(out_11), .B(4'b0001));  // open: out_5

  // Notes on the sheet:
  //   contents of rom_1 (hex, n*v repeats v):
  //   0 1 2 3 4 5 6 7
endmodule

module register_file (
  input  clr_registers,
  input  [1:0] in_2,
  input  in_3,
  input  [1:0] in_4,
  input  [3:0] in_5,
  input  [1:0] in_6,
  input  in_7,
  input  in_8,
  output [3:0] out_9,
  output [3:0] Read_reg_2
);

  wire decoder_1_out0, decoder_1_out1, decoder_1_out2, decoder_1_out3;
  wire [3:0] register_1_q, register_2_q, register_3_q, register_4_q;

  Decoder #(.select(2)) decoder_1 (
    .out0(decoder_1_out0), .out1(decoder_1_out1), .out2(decoder_1_out2), .out3(decoder_1_out3), .sel(in_4),
    .en(in_3));
  Register #(.width(4)) register_1 (.D(in_5), .en(decoder_1_out0), .Q(register_1_q), .clk(in_8), .clr(clr_registers));
  Register #(.width(4)) register_2 (.D(in_5), .en(decoder_1_out1), .Q(register_2_q), .clk(in_8), .clr(clr_registers));
  Register #(.width(4)) register_3 (.D(in_5), .en(decoder_1_out2), .Q(register_3_q), .clk(in_8), .clr(clr_registers));
  Register #(.width(4)) register_4 (.D(in_5), .en(decoder_1_out3), .Q(register_4_q), .clk(in_8), .clr(clr_registers));
  Multiplexer #(.select(2), .width(4)) multiplexer_1 (
    .in0(register_1_q), .in1(register_2_q), .in2(register_3_q), .in3(register_4_q), .out(out_9), .sel(in_2),
    .en(in_7));
  Multiplexer #(.select(2), .width(4)) multiplexer_2 (
    .in0(register_1_q), .in1(register_2_q), .in2(register_3_q), .in3(register_4_q), .out(Read_reg_2),
    .sel(in_6), .en(in_7));

  // Notes on the sheet:
  //   address of register
  //   WD
  //   Read reg1
endmodule

module _3_ripple_adder (
  input  C_IN,
  input  [2:0] A,
  input  [2:0] B,
  output [2:0] SUM,
  output out_5
);

  wire full_adder_1_c_out, full_adder_2_c_out;

  FULL_ADDER full_adder_1 (.C_IN(C_IN), .A(A[0]), .B(B[0]), .SUM(SUM[0]), .C_OUT(full_adder_1_c_out));
  FULL_ADDER full_adder_2 (.C_IN(full_adder_1_c_out), .A(A[1]), .B(B[1]), .SUM(SUM[1]), .C_OUT(full_adder_2_c_out));
  FULL_ADDER full_adder_3 (.C_IN(full_adder_2_c_out), .A(A[2]), .B(B[2]), .SUM(SUM[2]), .C_OUT(out_5));
endmodule

module _8_bit_adder_subtractor (
  input  C_in,
  input  B_invert,
  input  [7:0] in_3,
  input  [7:0] B,
  output [7:0] SUM,
  output out_6
);

  wire n4_bit_adder_subtractor_1_c_out;

  _4_bit_adder_subtractor u_4_bit_adder_subtractor_1 (
    .C_IN(C_in), .B_INV(B_invert), .C_OUT(n4_bit_adder_subtractor_1_c_out), .A(in_3[3:0]), .B(B[3:0]),
    .out_5(SUM[3:0]));
  _4_bit_adder_subtractor u_4_bit_adder_subtractor_2 (
    .C_IN(n4_bit_adder_subtractor_1_c_out), .B_INV(B_invert), .C_OUT(out_6), .A(in_3[7:4]), .B(B[7:4]),
    .out_5(SUM[7:4]));

  // Notes on the sheet:
  //   A
endmodule

module Program_counter (
  input  [3:0] in_1,
  input  brn,
  input  jmp,
  input  clock,
  input  [3:0] offset,
  input  clr,
  output [3:0] out_7
);

  wire not_1_out;
  wire [3:0] controlled_buffer_1_out, multiplexer_1_out, multiplexer_2_out, n4_bit_adder_1_sum,
       n4_bit_adder_2_sum;

  not not_1 (not_1_out, 1'b0);
  assign controlled_buffer_1_out = not_1_out ? multiplexer_2_out : 4'bz;  // Controlled_Buffer controlled_buffer_1
  assign in_1 = 1'b0 ? controlled_buffer_1_out : 4'bz;  // Controlled_Buffer controlled_buffer_2
  Register #(.width(4)) register_1 (.D(controlled_buffer_1_out), .Q(out_7), .clk(clock), .clr(clr));  // open: en
  _4_bit_adder u_4_bit_adder_1 (.SUM(n4_bit_adder_1_sum), .in_1(1'b0), .A(out_7), .B(4'b0001));  // open: out_5
  _4_bit_adder u_4_bit_adder_2 (
    .SUM(n4_bit_adder_2_sum), .in_1(1'b0), .A(n4_bit_adder_1_sum), .B(offset));  // open: out_5
  Multiplexer #(.width(4), .enable("false")) multiplexer_1 (
    .in0(n4_bit_adder_1_sum), .in1(n4_bit_adder_2_sum), .out(multiplexer_1_out), .sel(brn));
  Multiplexer #(.width(4), .enable("false")) multiplexer_2 (
    .in0(multiplexer_1_out), .in1(offset), .out(multiplexer_2_out), .sel(jmp));

  // Notes on the sheet:
  //   enable
endmodule

module PROJECT (
  input  [3:0] in_1,
  input  in_2,
  input  [1:0] in_3,
  input  [3:0] in_4,
  input  in_5,
  input  in_6,
  input  in_7,
  output [3:0] out_8,
  output [15:0] out_9,
  output [1:0] out_10,
  output [3:0] out_11,
  output [3:0] out_12,
  output [3:0] out_13
);

  wire [1:0] multiplexer_1_out;
  wire [3:0] multiplexer_2_out, n4_bit_alu_1_out_6, program_counter_1_out_7, register_file_1_read_reg_2;
  wire [11:0] controller_1_out_2;

  Program_counter program_counter_1 (
    .in_1(in_4), .clock(in_5), .clr(in_6), .out_7(program_counter_1_out_7), .offset(out_9[3:0]),
    .brn(controller_1_out_2[1]), .jmp(controller_1_out_2[0]));
  controller controller_1 (.in_1(out_9[11:8]), .out_2(controller_1_out_2));
  IM im_1 (.in_1(program_counter_1_out_7), .out_2(out_9));
  Multiplexer #(.width(2), .enable("false")) multiplexer_1 (
    .in0(out_9[5:4]), .in1(out_9[3:2]), .out(multiplexer_1_out), .sel(controller_1_out_2[7]));
  register_file register_file_1 (
    .in_4(multiplexer_1_out), .in_5(out_12), .in_8(in_5), .clr_registers(in_2), .out_9(out_8),
    .in_2(out_9[7:6]), .Read_reg_2(register_file_1_read_reg_2), .in_6(out_9[5:4]),
    .in_3(controller_1_out_2[6]), .in_7(controller_1_out_2[6]));
  Multiplexer #(.width(4), .enable("false")) multiplexer_2 (
    .in0(register_file_1_read_reg_2), .in1(out_9[3:0]), .out(multiplexer_2_out), .sel(controller_1_out_2[5]));
  _4_bit_ALU u_4_bit_alu_1 (
    .C_in(controller_1_out_2[9]), .in_2(controller_1_out_2[11:10]), .A(out_8), .B_inv(controller_1_out_2[8]),
    .B(multiplexer_2_out), .out_6(n4_bit_alu_1_out_6));  // open: ZF, OF, SF, CF
  DM dm_1 (
    .in_1(n4_bit_alu_1_out_6), .in_2(register_file_1_read_reg_2), .in_3(controller_1_out_2[4]),
    .in_5(controller_1_out_2[3]), .in_6(in_5), .out_7(out_11), .in_4(controller_1_out_2[4]));
  Multiplexer #(.width(4), .enable("false")) multiplexer_3 (
    .in0(n4_bit_alu_1_out_6), .in1(out_11), .out(out_12), .sel(controller_1_out_2[2]));

  assign out_10 = out_9[3:2];
  assign out_13 = out_9[3:0];

  // Notes on the sheet:
  //   Rdst
  //   Asrc
  //   M2R
endmodule

module IM (
  input  [3:0] in_1,
  output [15:0] out_2
);

  ROM #(.addrWidth(4), .dataWidth(16)) rom_1 (.addr(in_1), .data(out_2));  // open: sel

  // Notes on the sheet:
  //   contents of rom_1 (hex, n*v repeats v):
  //   e10 e21 86c bc2 36c c07 26c f32
endmodule

module DM (
  input  [3:0] in_1,
  input  [3:0] in_2,
  input  in_3,
  input  in_4,
  input  in_5,
  input  in_6,
  output [3:0] out_7
);

  RAM #(.addrWidth(4), .dataWidth(4), .bus("separate")) ram_1 (
    .addr(in_1), .din(in_2), .data(out_7), .str(in_3), .sel(in_4), .clk(in_6), .ld(in_5));  // open: clr
endmodule

module controller (
  input  [3:0] in_1,
  output [11:0] out_2
);

  ROM #(.addrWidth(4), .dataWidth(12)) rom_1 (.addr(in_1), .data(out_2), .sel(1'b1));

  // Notes on the sheet:
  //   contents of rom_1 (hex, n*v repeats v):
  //   c0 4c0 8c0 bc0 e0 4e0 8e0 be0 fc0 fe0 0 802 1 0 86c 830
endmodule
