// Logisim project COAL_LAB_11(DATA READ & WRITE)(JUST ONCE).circ as structural Verilog: 1 circuit, main circuit main
module main (
  input  CLK,
  input  CLR,
  input  [1:0] RD_Add1,
  input  [3:0] in_4,
  input  [1:0] WR_Add,
  input  [1:0] RD_Add2,
  input  RD____WR,
  output [3:0] RD_Data1,
  output [3:0] RD_Data2
);

  wire not_1_out;
  wire [3:0] demultiplexer_1_out0, demultiplexer_1_out1, demultiplexer_1_out2, demultiplexer_1_out3,
       register_1_q, register_2_q, register_3_q, register_4_q;

  Demultiplexer #(.select(2), .width(4)) demultiplexer_1 (
    .out0(demultiplexer_1_out0), .out1(demultiplexer_1_out1), .out2(demultiplexer_1_out2),
    .out3(demultiplexer_1_out3), .in(in_4), .sel(WR_Add), .en(RD____WR));
  Register #(.width(4)) register_1 (.D(demultiplexer_1_out0), .Q(register_1_q), .clk(CLK), .clr(CLR));  // open: en
  Register #(.width(4)) register_2 (.D(demultiplexer_1_out1), .Q(register_2_q), .clk(CLK), .clr(CLR));  // open: en
  Register #(.width(4)) register_3 (.D(demultiplexer_1_out2), .Q(register_3_q), .clk(CLK), .clr(CLR));  // open: en
  Register #(.width(4)) register_4 (.D(demultiplexer_1_out3), .Q(register_4_q), .clk(CLK), .clr(CLR));  // open: en
  not not_1 (not_1_out, RD____WR);
  Multiplexer #(.select(2), .width(4)) multiplexer_1 (
    .in0(register_1_q), .in1(register_2_q), .in2(register_3_q), .in3(register_4_q), .out(RD_Data1),
    .sel(RD_Add1), .en(not_1_out));
  Multiplexer #(.select(2), .width(4)) multiplexer_2 (
    .in0(register_1_q), .in1(register_2_q), .in2(register_3_q), .in3(register_4_q), .out(RD_Data2),
    .sel(RD_Add2), .en(not_1_out));
endmodule
