// Logisim project COAL_LAB_7        (8-BIT FULL ADDER).circ as structural Verilog: 6 circuits, main circuit main
module main (
  input  [3:0] in_1,
  input  in_2,
  output [1:0] out_3,
  output [1:0] out_4
);

  LED led_1 (.in(in_2));
  _7_Segment_Display u_7_segment_display_1 ();  // open: g, f, a, b, e, d, c, dp

  assign out_3 = in_1[3:2];
  assign out_4 = in_1[1:0];
endmodule

module _1bit_HA (
  input  A,
  input  B,
  output Sum,
  output C
);

  xor XOR (Sum, A, B);
  and AND (C, A, B);
endmodule

module _1bit_FA (
  input  A,
  input  B,
  input  C,
  output Sum,
  output Carry
);

  wire n1bit_ha_1_c, n1bit_ha_1_sum, n1bit_ha_2_c;

  _1bit_HA u_1bit_ha_1 (.A(A), .B(B), .Sum(n1bit_ha_1_sum), .C(n1bit_ha_1_c));
  _1bit_HA u_1bit_ha_2 (.A(n1bit_ha_1_sum), .B(C), .Sum(Sum), .C(n1bit_ha_2_c));
  or OR (Carry, n1bit_ha_2_c, n1bit_ha_1_c);
endmodule

module _4bit_FA (
  input  in_1,
  input  in_2,
  input  in_3,
  input  in_4,
  input  in_5,
  input  in_6,
  input  in_7,
  input  in_8,
  input  in_9,
  output out_10,
  output out_11,
  output out_12,
  output out_13,
  output out_14
);

  wire n1bit_fa_1_carry, n1bit_fa_2_carry, n1bit_fa_3_carry;

  _1bit_FA u_1bit_fa_1 (.A(in_2), .B(in_3), .C(in_1), .Sum(out_10), .Carry(n1bit_fa_1_carry));
  _1bit_FA u_1bit_fa_2 (.A(in_4), .B(in_5), .C(n1bit_fa_1_carry), .Sum(out_11), .Carry(n1bit_fa_2_carry));
  _1bit_FA u_1bit_fa_3 (.A(in_6), .B(in_7), .C(n1bit_fa_2_carry), .Sum(out_12), .Carry(n1bit_fa_3_carry));
  _1bit_FA u_1bit_fa_4 (.A(in_8), .B(in_9), .C(n1bit_fa_3_carry), .Sum(out_13), .Carry(out_14));
endmodule

module _1bit_ALU (
  input  Cin,
  input  [1:0] Op,
  input  A,
  input  B,
  input  CF,
  output Result
);

  wire AND_out, n1bit_fa_1_sum, OR_out;

  and AND (AND_out, A, B);
  or OR (OR_out, A, B);
  _1bit_FA u_1bit_fa_1 (.A(A), .B(B), .C(Cin), .Sum(n1bit_fa_1_sum), .Carry(CF));
  Multiplexer #(.select(2), .enable("false")) multiplexer_1 (
    .in0(AND_out), .in1(OR_out), .in2(n1bit_fa_1_sum), .in3(1'b0), .out(Result), .sel(Op));
endmodule

module _8bit_FA (
  input  in_1,
  input  [3:0] in_2,
  input  [3:0] in_3,
  input  [3:0] in_4,
  input  [3:0] in_5,
  output [7:0] out_6,
  output out_7
);

  wire n4bit_fa_1_out_14;

  _4bit_FA u_4bit_fa_1 (
    .in_2(in_2[0]), .in_3(in_3[0]), .in_4(in_2[1]), .in_5(in_3[1]), .in_6(in_2[2]), .in_7(in_3[2]),
    .in_8(in_2[3]), .in_9(in_3[3]), .out_10(out_6[0]), .out_11(out_6[1]), .out_12(out_6[2]),
    .out_13(out_6[3]), .out_14(n4bit_fa_1_out_14), .in_1(in_1));
  _4bit_FA u_4bit_fa_2 (
    .in_2(in_4[0]), .in_3(in_5[0]), .in_4(in_4[1]), .in_5(in_5[1]), .in_6(in_4[2]), .in_7(in_5[2]),
    .in_8(in_4[3]), .in_9(in_5[3]), .out_10(out_6[4]), .out_11(out_6[5]), .out_12(out_6[6]),
    .out_13(out_6[7]), .out_14(out_7), .in_1(n4bit_fa_1_out_14));
endmodule
