// Logisim project 1 bit comparator.circ as structural Verilog
module half_adder (
  input  A,
  input  B,
  output SUM,
  output CARRY
);

  xor xor_1 (SUM, A, B);
  and and_1 (CARRY, A, B);

  // Notes on the sheet:
  //   Half Adder 
endmodule

module full_adder (
  input  A,
  input  B,
  input  Cin,
  output Sum,
  output Carry
);

  wire and_1_out, half_adder_1_carry, half_adder_1_sum;

  half_adder half_adder_1 (.A(A), .B(B), .SUM(half_adder_1_sum), .CARRY(half_adder_1_carry));
  and and_1 (and_1_out, half_adder_1_carry, Cin);
  xor xor_1 (Sum, half_adder_1_sum, Cin);
  or or_1 (Carry, and_1_out, half_adder_1_carry);

  // Notes on the sheet:
  //   Full Adder 
endmodule

module adder_subtractor (
  input  Cin,
  input  A,
  input  B,
  output Sum_Sub,
  output C_out
);

  wire xor_1_out;

  xor xor_1 (xor_1_out, Cin, B);
  full_adder full_adder_1 (.A(Cin), .B(A), .Cin(xor_1_out), .Sum(Sum_Sub), .Carry(C_out));

  // Notes on the sheet:
  //   Adder Subtractor
endmodule

module _1_bit_comparator (
  input  A,
  input  B,
  output A_B,
  output A_B_2,
  output A_B_3
);

  wire not_1_out, not_2_out;

  not not_1 (not_1_out, A);
  not not_2 (not_2_out, B);
  and and_1 (A_B, not_1_out, B);
  and and_2 (A_B_3, A, not_2_out);
  nor nor_1 (A_B_2, A_B, A_B_3);
endmodule

module _1bit_alu (
  input  cin,
  input  A,
  input  B,
  input  [1:0] in_4,
  input  in_5,
  output out_6,
  output out_7,
  output out_8,
  output out_9
);

  wire adder_subtractor_1_c_out, and_1_out, or_1_out;

  adder_subtractor adder_subtractor_1 (.Cin(cin), .A(A), .B(B), .C_out(adder_subtractor_1_c_out));  // open: Sum_Sub
  _1_bit_comparator _1_Bit_Comparator (.A(A), .B(B), .A_B(out_7), .A_B_2(out_8), .A_B_3(out_9));
  and and_1 (and_1_out, A, B);
  or or_1 (or_1_out, A, B);
  Multiplexer #(.select(2)) multiplexer_1 (
    .in0(and_1_out), .in1(or_1_out), .in2(adder_subtractor_1_c_out), .out(out_6), .sel(in_4), .en(in_5));  // open: in3
endmodule
