// Logisim project ALU(1-4 Bit),RAM & ROM.circ as structural Verilog: 6 circuits, main circuit main
// h.a
module main (
  input  A,
  input  B,
  output Sum,
  output Carry
);

  xor xor_1 (Sum, A, B);
  and and_1 (Carry, A, B);
endmodule

// FA
module full_adder (
  input  in_1,
  input  in_2,
  input  in_3,
  output out_4,
  output out_5
);

  wire and_out, main_1_carry, main_1_sum;

  main main_1 (.A(in_1), .B(in_2), .Sum(main_1_sum), .Carry(main_1_carry));
  and \and  (and_out, main_1_sum, in_3);
  xor \xor  (out_4, main_1_sum, in_3);
  or \or  (out_5, and_out, main_1_carry);
endmodule

// ALU
module _1_bit_alu (
  input  Cin,
  input  Bin,
  input  [1:0] OP,
  input  A,
  input  B,
  output Output,
  output Cout
);

  wire AND_out, full_adder_1_out_4, multiplexer_1_out, not_1_out, OR_out;

  Multiplexer multiplexer_1 (.in0(B), .in1(not_1_out), .out(multiplexer_1_out), .sel(Bin));  // open: en
  not not_1 (not_1_out, B);
  and AND (AND_out, A, B);
  or OR (OR_out, A, B);
  full_adder full_adder_1 (.in_1(Cin), .in_2(A), .in_3(multiplexer_1_out), .out_4(full_adder_1_out_4), .out_5(Cout));
  Multiplexer #(.select(2), .enable("false")) multiplexer_2 (
    .in0(AND_out), .in1(OR_out), .in2(full_adder_1_out_4), .out(Output), .sel(OP));  // open: in3
endmodule

module _4_bit_alu (
  input  Cin,
  input  Binv,
  input  [1:0] OP,
  input  [3:0] in_4,
  input  [3:0] in_5,
  output [3:0] Output,
  output Z_F,
  output S_F,
  output O_F,
  output C_F
);

  wire n1_bit_alu_1_cout, n1_bit_alu_2_cout, n1_bit_alu_3_cout;

  _1_bit_alu u_1_bit_alu_1 (
    .A(in_4[0]), .B(in_5[0]), .Output(Output[0]), .Bin(Cin), .Cin(Binv), .OP(OP), .Cout(n1_bit_alu_1_cout));
  _1_bit_alu u_1_bit_alu_2 (
    .A(in_4[1]), .B(in_5[1]), .Output(Output[1]), .Bin(Cin), .Cin(n1_bit_alu_1_cout), .OP(OP),
    .Cout(n1_bit_alu_2_cout));
  _1_bit_alu u_1_bit_alu_3 (
    .A(in_4[2]), .B(in_5[2]), .Output(Output[2]), .Bin(Cin), .Cin(n1_bit_alu_2_cout), .OP(OP),
    .Cout(n1_bit_alu_3_cout));
  _1_bit_alu u_1_bit_alu_4 (
    .A(in_4[3]), .B(in_5[3]), .Output(Output[3]), .Bin(Cin), .Cin(n1_bit_alu_3_cout), .OP(OP), .Cout(C_F));
  xor XOR (O_F, n1_bit_alu_3_cout, C_F);
  nor XNOR (Z_F, Output[0], Output[1], Output[2], Output[3]);

  assign S_F = Output[3];
endmodule

module check (
  input  [2:0] Input,
  input  Enable,
  input  CLK,
  input  Selection,
  input  Reset,
  output [3:0] Output
);

  wire [2:0] counter_1_q;

  Counter #(.width(3), .max('h7)) counter_1 (
    .D(Input), .count(Enable), .Q(counter_1_q), .clk(CLK), .clr(Reset));  // open: load, carry
  ROM #(.addrWidth(3), .dataWidth(4)) rom_1 (.addr(counter_1_q), .data(Output), .sel(Selection));

  // Notes on the sheet:
  //   Counter
  //   ROM
endmodule

module Check_Ram (
  input  [2:0] Address,
  input  [3:0] Data_Input,
  input  Store,
  input  Select,
  input  CLR,
  input  [3:0] in_6,
  input  CLK,
  input  Load,
  output [3:0] Output
);

  wire not_1_out;

  RAM #(.addrWidth(3), .dataWidth(4), .bus("separate")) ram_1 (
    .addr(Address), .din(Data_Input), .data(Output), .str(Store), .sel(Select), .clk(CLK), .ld(not_1_out),
    .clr(CLR));
  not not_1 (not_1_out, Load);
  Controlled_Buffer #(.width(4)) controlled_buffer_1 (.in(in_6), .en(Load));  // open: out

  // Notes on the sheet:
  //   RAM
endmodule
