// Logisim project ALU.circ as structural Verilog: 3 circuits, main circuit main
module main (
  input  Cin,
  input  A,
  input  B,
  input  [1:0] in_4,
  input  in_5,
  output out_6,
  output out_7
);

  wire adder_subtracter_1_sum_sub, and_1_out, or_1_out;

  Adder_Subtracter adder_subtracter_1 (.cin(Cin), .A(A), .B(B), .sum_sub(adder_subtracter_1_sum_sub), .c_out(out_7));
  and and_1 (and_1_out, A, B);
  or or_1 (or_1_out, A, B);
  Multiplexer #(.select(2)) multiplexer_1 (
    .in0(and_1_out), .in1(or_1_out), .in2(adder_subtracter_1_sum_sub), .out(out_6), .sel(in_4), .en(in_5));  // open: in3

  // Notes on the sheet:
  //   Adder/Subtractor
endmodule

module ALU (
  input  Carry_In,
  input  A,
  input  B,
  input  in_4,
  input  [1:0] in_5,
  output out_6,
  output out_7
);

  wire adder_subtracter_1_sum_sub, and_1_out, or_1_out;

  Adder_Subtracter adder_subtracter_1 (
    .cin(Carry_In), .A(A), .B(B), .sum_sub(adder_subtracter_1_sum_sub), .c_out(out_7));
  and and_1 (and_1_out, A, B);
  or or_1 (or_1_out, A, B);
  Multiplexer #(.select(2)) multiplexer_1 (
    .in0(and_1_out), .in1(or_1_out), .in2(adder_subtracter_1_sum_sub), .out(out_6), .sel(in_5), .en(in_4));  // open: in3

  // Notes on the sheet:
  //   Adder/Subtractor
endmodule

module Adder_Subtracter (
  input  cin,
  input  A,
  input  B,
  output sum_sub,
  output c_out
);

  wire xor_1_out;

  xor xor_1 (xor_1_out, cin, B);
  full_adder full_adder_1 (.A(cin), .B(A), .Cin(xor_1_out), .Sum(sum_sub), .Carry(c_out));
endmodule
