// Logisim project Program Counter.circ as structural Verilog: 1 circuit, main circuit main
module main (
  input  in_1,
  input  in_2,
  output [3:0] out_3
);

  wire [3:0] adder_1_out;

  Register #(.width(4)) register_1 (.D(adder_1_out), .Q(out_3), .clk(in_1), .clr(in_2));  // open: en
  Adder #(.width(4)) adder_1 (.a(4'b0011), .b(out_3), .out(adder_1_out));  // open: cin, cout
endmodule
