// Logisim project ROM.circ as structural Verilog: 8 circuits, main circuit main
// h.a
module main (
  input  in_1,
  input  in_2,
  output out_3,
  output out_4
);

  xor xor_1 (out_3, in_1, in_2);
  and and_1 (out_4, in_1, in_2);
endmodule

// FA
module full_adder (
  input  A,
  input  B,
  input  Cin,
  output Sum,
  output Carry
);

  wire and_out, main_1_out_3, main_1_out_4;

  main main_1 (.in_1(A), .in_2(B), .out_3(main_1_out_3), .out_4(main_1_out_4));
  and \and  (and_out, main_1_out_3, Cin);
  or \or  (Carry, and_out, main_1_out_4);
  xor \xor  (Sum, main_1_out_3, Cin);
endmodule

// ALU
module _1_bit_alu (
  input  Bin,
  input  Cin,
  input  A,
  input  [1:0] OP,
  input  B,
  output Output,
  output Cout
);

  wire AND_out, full_adder_1_sum, multiplexer_1_out, not_1_out, OR_out;

  Multiplexer multiplexer_1 (.in0(B), .in1(not_1_out), .out(multiplexer_1_out), .sel(Bin));  // open: en
  not not_1 (not_1_out, B);
  and AND (AND_out, A, B);
  or OR (OR_out, A, B);
  full_adder full_adder_1 (.A(Cin), .B(A), .Cin(multiplexer_1_out), .Sum(full_adder_1_sum), .Carry(Cout));
  Multiplexer #(.select(2), .enable("false")) multiplexer_2 (
    .in0(AND_out), .in1(OR_out), .in2(full_adder_1_sum), .out(Output), .sel(OP));  // open: in3
endmodule

module _4_bit_alu (
  input  Cin,
  input  Binv,
  input  [1:0] OP,
  input  [3:0] in_4,
  input  [3:0] in_5,
  output [3:0] Output,
  output Z_F,
  output S_F,
  output O_F,
  output C_F
);

  wire n1_bit_alu_1_cout, n1_bit_alu_2_cout, n1_bit_alu_3_cout;

  _1_bit_alu u_1_bit_alu_1 (
    .A(in_4[0]), .B(in_5[0]), .Output(Output[0]), .Bin(Cin), .Cin(Binv), .OP(OP), .Cout(n1_bit_alu_1_cout));
  _1_bit_alu u_1_bit_alu_2 (
    .A(in_4[1]), .B(in_5[1]), .Output(Output[1]), .Bin(Cin), .Cin(n1_bit_alu_1_cout), .OP(OP),
    .Cout(n1_bit_alu_2_cout));
  _1_bit_alu u_1_bit_alu_3 (
    .A(in_4[2]), .B(in_5[2]), .Output(Output[2]), .Bin(Cin), .Cin(n1_bit_alu_2_cout), .OP(OP),
    .Cout(n1_bit_alu_3_cout));
  _1_bit_alu u_1_bit_alu_4 (
    .A(in_4[3]), .B(in_5[3]), .Output(Output[3]), .Bin(Cin), .Cin(n1_bit_alu_3_cout), .OP(OP), .Cout(C_F));
  xor XOR (O_F, n1_bit_alu_3_cout, C_F);
  nor XNOR (Z_F, Output[0], Output[1], Output[2], Output[3]);

  assign S_F = Output[3];
endmodule

module check (
  input  [2:0] Data,
  input  Count,
  input  CLK,
  input  Select,
  input  CLR,
  output [3:0] out_6
);

  wire [2:0] counter_1_q;

  Counter #(.width(3), .max('h7)) counter_1 (
    .D(Data), .count(Count), .Q(counter_1_q), .clk(CLK), .clr(CLR));  // open: load, carry
  ROM #(.addrWidth(3), .dataWidth(4)) rom_1 (.addr(counter_1_q), .data(out_6), .sel(Select));

  // Notes on the sheet:
  //   ROM
endmodule

module Check_Ram (
  input  [2:0] Address,
  input  [3:0] Data_Input,
  input  Store,
  input  Select,
  input  CLR,
  input  CLK,
  input  in_7,
  input  [3:0] in_8,
  output [3:0] out_9
);

  wire not_1_out;

  RAM #(.addrWidth(3), .dataWidth(4), .bus("separate")) ram_1 (
    .addr(Address), .din(Data_Input), .data(out_9), .str(Store), .sel(Select), .clk(CLK), .ld(not_1_out),
    .clr(CLR));
  not not_1 (not_1_out, in_7);
  assign out_9 = in_7 ? in_8 : 4'bz;  // Controlled_Buffer controlled_buffer_1

  // Notes on the sheet:
  //   RAM
endmodule

module LAB_11 (
  input  [2:0] in_1,
  input  [2:0] in_2,
  input  [3:0] in_3,
  input  in_4,
  input  in_5,
  input  in_6,
  input  in_7,
  input  [3:0] in_8,
  output [3:0] out_9
);

  wire [2:0] counter_1_q;
  wire [3:0] rom_1_data;

  Counter #(.width(3), .max('h7)) counter_1 (
    .D(in_2), .count(in_4), .Q(counter_1_q), .clk(in_5));  // open: load, carry, clr
  // XOR_Gate xor_1 has open pins: in0=rom_1_data, in1=in_8, out=open
  ROM #(.addrWidth(3), .dataWidth(4)) rom_1 (.addr(counter_1_q), .data(rom_1_data));  // open: sel
  RAM #(.addrWidth(3), .dataWidth(4), .bus("separate")) ram_1 (
    .addr(in_1), .din(in_3), .data(out_9), .clk(in_5), .ld(in_7), .clr(in_6));  // open: str, sel
  assign out_9 = in_7 ? rom_1_data : 4'bz;  // Controlled_Buffer controlled_buffer_1
endmodule

module Half_adder (
  input  [3:0] in_1,
  input  [3:0] in_2,
  output [3:0] out_3,
  output [3:0] out_4
);

  assign out_3 = in_1 | in_2;  // OR_Gate or_1, 4 bits wide
  assign out_4 = in_2 & in_1;  // AND_Gate and_1, 4 bits wide
endmodule
