// Logisim project Register_File.circ as structural Verilog
module Lab_11 (
  input  [7:0] Input,
  input  Enable,
  input  Reset,
  input  CLK,
  output [7:0] Output
);

  Register register_1 (.D(Input), .en(Enable), .Q(Output), .clk(CLK), .clr(Reset));

  // Notes on the sheet:
  //   Register
endmodule

module LAB_01_Task (
  input  [1:0] Read_Add2,
  input  [1:0] Read_Add1,
  input  [3:0] in_3,
  input  CLR,
  input  CLK,
  input  [1:0] Write_address,
  input  Read_Write,
  output [3:0] Read_data_1,
  output [3:0] Read_data_02
);

  wire decoder_1_out0, decoder_1_out1, decoder_1_out2, decoder_1_out3, not_1_out;
  wire [3:0] register_1_q, register_2_q, register_3_q, register_4_q;

  not not_1 (not_1_out, Read_Write);
  Decoder #(.select(2), .disabled(0)) decoder_1 (
    .out0(decoder_1_out0), .out1(decoder_1_out1), .out2(decoder_1_out2), .out3(decoder_1_out3),
    .sel(Write_address), .en(Read_Write));
  Multiplexer #(.select(2), .width(4)) multiplexer_1 (
    .in0(register_1_q), .in1(register_2_q), .in2(register_3_q), .in3(register_4_q), .out(Read_data_1),
    .sel(Read_Add1), .en(not_1_out));
  Register #(.width(4)) register_1 (.D(in_3), .en(decoder_1_out0), .Q(register_1_q), .clk(CLK), .clr(CLR));
  Register #(.width(4)) register_2 (.D(in_3), .en(decoder_1_out1), .Q(register_2_q), .clk(CLK), .clr(CLR));
  Multiplexer #(.select(2), .width(4)) multiplexer_2 (
    .in0(register_1_q), .in1(register_2_q), .in2(register_3_q), .in3(register_4_q), .out(Read_data_02),
    .sel(Read_Add2), .en(not_1_out));
  Register #(.width(4)) register_3 (.D(in_3), .en(decoder_1_out2), .Q(register_3_q), .clk(CLK), .clr(CLR));
  Register #(.width(4)) register_4 (.D(in_3), .en(decoder_1_out3), .Q(register_4_q), .clk(CLK), .clr(CLR));
endmodule

module Register_File (
  input  [1:0] Read_Add1,
  input  [1:0] Read_Add2,
  input  [1:0] Write_address,
  input  [3:0] Write_Data,
  input  CLR,
  input  Reg_WR,
  input  CLK,
  output [3:0] Read_data_1,
  output [3:0] Read_data_02
);

  wire and_1_out, and_2_out, and_3_out, and_4_out, and_5_out, decoder_1_out0, decoder_1_out1, decoder_1_out2,
       decoder_1_out3, not_1_out;
  wire [3:0] register_1_q, register_2_q, register_3_q, register_4_q;

  Decoder #(.select(2), .enable("false")) decoder_1 (
    .out0(decoder_1_out0), .out1(decoder_1_out1), .out2(decoder_1_out2), .out3(decoder_1_out3),
    .sel(Write_address));
  and and_1 (and_1_out, Reg_WR, CLK);
  and and_2 (and_2_out, decoder_1_out0, and_1_out);
  and and_3 (and_3_out, decoder_1_out1, and_1_out);
  and and_4 (and_4_out, decoder_1_out2, and_1_out);
  and and_5 (and_5_out, decoder_1_out3, and_1_out);
  Register #(.width(4)) register_1 (.D(Write_Data), .Q(register_1_q), .clk(and_2_out), .clr(not_1_out));  // open: en
  Register #(.width(4)) register_2 (.D(Write_Data), .Q(register_2_q), .clk(and_3_out), .clr(not_1_out));  // open: en
  Register #(.width(4)) register_3 (.D(Write_Data), .Q(register_3_q), .clk(and_4_out), .clr(not_1_out));  // open: en
  Register #(.width(4)) register_4 (.D(Write_Data), .Q(register_4_q), .clk(and_5_out), .clr(not_1_out));  // open: en
  not not_1 (not_1_out, CLR);
  Multiplexer #(.select(2), .width(4), .enable("false")) multiplexer_1 (
    .in0(register_1_q), .in1(register_2_q), .in2(register_3_q), .in3(register_4_q), .out(Read_data_1),
    .sel(Read_Add1));
  Multiplexer #(.select(2), .width(4), .enable("false")) multiplexer_2 (
    .in0(register_1_q), .in1(register_2_q), .in2(register_3_q), .in3(register_4_q), .out(Read_data_02),
    .sel(Read_Add2));
endmodule

module Controller (
  input  Op5,
  input  Op4,
  input  Op3,
  input  Op2,
  input  Op1,
  input  Op0,
  output Reg_Dis,
  output ALUsrc,
  output Mem_to_Reg,
  output RegWrite,
  output MemRead,
  output MemWrite,
  output Branch,
  output ALUOp1,
  output ALUOp2
);

  wire undriven;

  and and_1 (ALUOp1, Op5, Op4, Op3, Op2, Op1, Op0);
  and and_2 (Mem_to_Reg, Op5, Op4, Op3, Op2, Op1, Op0);
  and and_3 (MemWrite, Op5, Op4, Op3, Op2, Op1, Op0);
  and and_4 (ALUOp2, Op5, Op4, Op3, Op2, Op1, Op0);
  or or_1 (ALUsrc, Mem_to_Reg, MemWrite);
  or or_2 (RegWrite, ALUOp1, Mem_to_Reg);
  // Probe on undriven

  assign Branch = ALUOp2;
  assign MemRead = Mem_to_Reg;
  assign Reg_Dis = ALUOp1;

  // Notes on the sheet:
  //   R_Format
  //   LW
  //   SW
endmodule
