// Logisim project Project.circ as structural Verilog: 17 circuits, main circuit main
module main (
  input  CLR,
  output [15:0] out_2
);

  wire and_1_out, CLK_out, n4_bit_alu_1_zf, not_1_out, or_1_out;
  wire [1:0] multiplexer_1_out;
  wire [3:0] adder_1_out, adder_2_out, data_memory_1_read_data, multiplexer_2_out, multiplexer_3_out,
       multiplexer_4_out, multiplexer_5_out, n4_bit_alu_1_out_6, register_1_q, register_file_1_read_data1,
       register_file_1_read_data2;
  wire [15:0] control_unit_1_out;

  Register #(.width(4)) register_1 (
    .D(multiplexer_4_out), .Q(register_1_q), .clk(CLK_out), .clr(not_1_out));  // open: en
  Clock CLK (.out(CLK_out));
  not not_1 (not_1_out, CLR);
  Adder #(.width(4)) adder_1 (.a(register_1_q), .b(4'b0001), .out(adder_1_out));  // open: cin, cout
  Instruction_Memory instruction_memory_1 (.Address(register_1_q), .Instruction(out_2));
  Multiplexer #(.width(2), .enable("false")) multiplexer_1 (
    .in0(out_2[5:4]), .in1(out_2[3:2]), .out(multiplexer_1_out), .sel(control_unit_1_out[4]));
  or or_1 (or_1_out, control_unit_1_out[7], CLK_out);
  Register_File register_file_1 (
    .Write_Address(multiplexer_1_out), .Write_Data(multiplexer_5_out),
    .Read_Data2(register_file_1_read_data2), .Rd0___Wr1(or_1_out), .CLR(CLR),
    .Read_Data1(register_file_1_read_data1), .Rd1(out_2[7:6]), .Rd2(out_2[5:4]), .Clock(CLK_out));
  Control_Unit control_unit_1 (.in(out_2[11:8]), .out(control_unit_1_out));
  Multiplexer #(.width(4), .enable("false")) multiplexer_2 (
    .in0(register_file_1_read_data2), .in1(out_2[3:0]), .out(multiplexer_2_out), .sel(control_unit_1_out[2]));
  Adder #(.width(4)) adder_2 (.a(adder_1_out), .b(out_2[3:0]), .out(adder_2_out));  // open: cin, cout
  _4_Bit_ALU u_4_bit_alu_1 (
    .in_3(register_file_1_read_data1), .in_4(multiplexer_2_out), .out_6(n4_bit_alu_1_out_6),
    .ZF(n4_bit_alu_1_zf), .Add0_Sub1(control_unit_1_out[9]), .Cin(control_unit_1_out[8]),
    .ALUop(control_unit_1_out[11:10]));  // open: SF, OF, CF
  and and_1 (and_1_out, control_unit_1_out[1], n4_bit_alu_1_zf);
  Multiplexer #(.width(4), .enable("false")) multiplexer_3 (
    .in0(adder_1_out), .in1(adder_2_out), .out(multiplexer_3_out), .sel(and_1_out));
  Data_Memory data_memory_1 (
    .Address(n4_bit_alu_1_out_6), .Write_Data(register_file_1_read_data2),
    .Read_Data(data_memory_1_read_data), .MRD(control_unit_1_out[6]), .MWR(control_unit_1_out[5]),
    .CLK(CLK_out), .CLR(CLR));
  Multiplexer #(.width(4), .enable("false")) multiplexer_4 (
    .in0(out_2[3:0]), .in1(multiplexer_3_out), .out(multiplexer_4_out), .sel(control_unit_1_out[0]));
  Multiplexer #(.width(4), .enable("false")) multiplexer_5 (
    .in0(data_memory_1_read_data), .in1(n4_bit_alu_1_out_6), .out(multiplexer_5_out),
    .sel(control_unit_1_out[3]));

  // Notes on the sheet:
  //   RegDst
  //   ALUSrc
  //   Branch
  //   Jmp
  //   MemToReg
endmodule

module _1bit_HA (
  input  A,
  input  B,
  output Y,
  output Cout
);

  xor XOR (Y, A, B);
  and AND (Cout, A, B);
endmodule

module _1bit_FA (
  input  A,
  input  B,
  input  C,
  output Sum,
  output Carry
);

  wire n1bit_ha_1_cout, n1bit_ha_1_y, n1bit_ha_2_cout;

  _1bit_HA u_1bit_ha_1 (.A(A), .B(B), .Y(n1bit_ha_1_y), .Cout(n1bit_ha_1_cout));
  _1bit_HA u_1bit_ha_2 (.A(n1bit_ha_1_y), .B(C), .Y(Sum), .Cout(n1bit_ha_2_cout));
  or OR (Carry, n1bit_ha_2_cout, n1bit_ha_1_cout);
endmodule

module _4bit_FA (
  input  in_1,
  input  in_2,
  input  in_3,
  input  in_4,
  input  in_5,
  input  in_6,
  input  in_7,
  input  in_8,
  input  in_9,
  output out_10,
  output out_11,
  output out_12,
  output out_13,
  output out_14
);

  wire n1bit_fa_1_carry, n1bit_fa_2_carry, n1bit_fa_3_carry;

  _1bit_FA u_1bit_fa_1 (.A(in_2), .B(in_3), .C(in_1), .Carry(n1bit_fa_1_carry), .Sum(out_10));
  _1bit_FA u_1bit_fa_2 (.A(in_4), .B(in_5), .C(n1bit_fa_1_carry), .Carry(n1bit_fa_2_carry), .Sum(out_11));
  _1bit_FA u_1bit_fa_3 (.A(in_6), .B(in_7), .C(n1bit_fa_2_carry), .Carry(n1bit_fa_3_carry), .Sum(out_12));
  _1bit_FA u_1bit_fa_4 (.A(in_8), .B(in_9), .C(n1bit_fa_3_carry), .Carry(out_14), .Sum(out_13));
endmodule

module _8bit_FA (
  input  in_1,
  input  [3:0] in_2,
  input  [3:0] in_3,
  input  [3:0] in_4,
  input  [3:0] in_5,
  output [7:0] out_6,
  output out_7
);

  wire n4bit_fa_1_out_14;

  _4bit_FA u_4bit_fa_1 (
    .in_2(in_2[0]), .in_3(in_3[0]), .in_4(in_2[1]), .in_5(in_3[1]), .in_6(in_2[2]), .in_7(in_2[3]),
    .in_8(in_2[3]), .in_9(in_3[3]), .out_10(out_6[0]), .out_11(out_6[1]), .out_12(out_6[2]),
    .out_13(out_6[3]), .in_1(in_1), .out_14(n4bit_fa_1_out_14));
  _4bit_FA u_4bit_fa_2 (
    .in_2(in_4[0]), .in_3(in_5[0]), .in_4(in_4[1]), .in_5(in_5[1]), .in_6(in_4[2]), .in_7(in_4[3]),
    .in_8(in_4[3]), .in_9(in_5[3]), .out_10(out_6[4]), .out_11(out_6[5]), .out_12(out_6[6]),
    .out_13(out_6[7]), .in_1(n4bit_fa_1_out_14), .out_14(out_7));

  assign in_3[2] = in_2[3];
  assign in_5[2] = in_4[3];

  // Notes on the sheet:
  //   8bit Full Adder
endmodule

module _1_Bit_ALU (
  input  Binv,
  input  Cin,
  input  A,
  input  B,
  input  in_5,
  input  [1:0] Op,
  output Result,
  output CF,
  output Set
);

  wire AND_out, multiplexer_1_out, not_1_out, OR_out;

  Multiplexer #(.enable("false")) multiplexer_1 (.in0(B), .in1(not_1_out), .out(multiplexer_1_out), .sel(Binv));
  not not_1 (not_1_out, B);
  _1bit_FA u_1bit_fa_1 (.A(A), .B(multiplexer_1_out), .C(Cin), .Carry(CF), .Sum(Set));
  and AND (AND_out, A, B);
  or OR (OR_out, A, B);
  Multiplexer #(.select(2), .enable("false")) multiplexer_2 (
    .in0(AND_out), .in1(OR_out), .in2(Set), .in3(in_5), .out(Result), .sel(Op));
endmodule

module _4_Bit_ALU (
  input  Add0_Sub1,
  input  Cin,
  input  [3:0] in_3,
  input  [3:0] in_4,
  input  [1:0] ALUop,
  output [3:0] out_6,
  output ZF,
  output SF,
  output OF,
  output CF
);

  wire n1_bit_alu_1_cf, n1_bit_alu_2_cf, n1_bit_alu_3_cf, n1_bit_alu_4_set;

  _1_Bit_ALU u_1_bit_alu_1 (
    .A(in_3[0]), .B(in_4[0]), .Result(out_6[0]), .CF(n1_bit_alu_1_cf), .Cin(Cin), .Binv(Add0_Sub1),
    .Op(ALUop), .in_5(n1_bit_alu_4_set));  // open: Set
  _1_Bit_ALU u_1_bit_alu_2 (
    .A(in_3[1]), .B(in_4[1]), .Result(out_6[1]), .CF(n1_bit_alu_2_cf), .Cin(n1_bit_alu_1_cf),
    .Binv(Add0_Sub1), .Op(ALUop), .in_5(1'b0));  // open: Set
  _1_Bit_ALU u_1_bit_alu_3 (
    .A(in_3[2]), .B(in_4[3]), .Result(out_6[2]), .CF(n1_bit_alu_3_cf), .Cin(n1_bit_alu_2_cf),
    .Binv(Add0_Sub1), .Op(ALUop), .in_5(1'b0));  // open: Set
  _1_Bit_ALU u_1_bit_alu_4 (
    .A(in_3[3]), .B(in_4[2]), .Result(out_6[3]), .CF(CF), .Cin(n1_bit_alu_3_cf), .Binv(Add0_Sub1),
    .Op(ALUop), .Set(n1_bit_alu_4_set), .in_5(1'b0));
  nor NOR (ZF, out_6[0], out_6[1], out_6[2], out_6[3]);
  xor XOR (OF, n1_bit_alu_3_cf, CF);

  assign SF = out_6[3];
endmodule

module RAM_with_RD_WR (
  input  [3:0] in_1,
  input  in_2,
  input  [2:0] in_3,
  input  in_4,
  input  in_5,
  input  in_6,
  input  in_7,
  input  clock,
  output [3:0] out_9
);

  wire [3:0] controlled_buffer_1_out;

  assign controlled_buffer_1_out = in_2 ? in_1 : 4'bz;  // Controlled_Buffer controlled_buffer_1
  RAM #(.addrWidth(3), .dataWidth(4)) ram_1 (
    .addr(in_3), .data(controlled_buffer_1_out), .sel(in_5), .clk(clock), .ld(in_6), .clr(in_7));
  assign out_9 = in_4 ? controlled_buffer_1_out : 4'bz;  // Controlled_Buffer controlled_buffer_2
endmodule

module ROM_with_Counter (
  input  in_1,
  input  [2:0] in_2,
  input  inc,
  input  clock,
  input  reset,
  output [3:0] out_6
);

  wire [2:0] counter_1_q;

  Counter #(.width(3), .max('h7)) counter_1 (
    .load(in_1), .D(in_2), .count(inc), .Q(counter_1_q), .clk(clock), .clr(reset));  // open: carry
  ROM #(.addrWidth(3), .dataWidth(4)) rom_1 (.addr(counter_1_q), .data(out_6));  // open: sel

  // Notes on the sheet:
  //   contents of rom_1 (hex, n*v repeats v):
  //   1 3 5 6 7 1 a c
endmodule

module Register_File (
  input  [1:0] Rd1,
  input  [1:0] Rd2,
  input  [1:0] Write_Address,
  input  [3:0] Write_Data,
  input  Clock,
  input  CLR,
  input  Rd0___Wr1,
  output [3:0] Read_Data1,
  output [3:0] Read_Data2
);

  wire and_1_out, and_2_out, and_3_out, and_4_out, and_5_out, decoder_1_out0, decoder_1_out1, decoder_1_out2,
       decoder_1_out3, not_1_out, not_2_out;
  wire [3:0] register_1_q, register_2_q, register_3_q, register_4_q;

  Decoder #(.select(2), .enable("false")) decoder_1 (
    .out0(decoder_1_out0), .out1(decoder_1_out1), .out2(decoder_1_out2), .out3(decoder_1_out3),
    .sel(Write_Address));
  and and_1 (and_1_out, not_1_out, Clock);
  not not_1 (not_1_out, Rd0___Wr1);
  and and_2 (and_2_out, decoder_1_out0, and_1_out);
  and and_3 (and_3_out, decoder_1_out1, and_1_out);
  and and_4 (and_4_out, decoder_1_out2, and_1_out);
  and and_5 (and_5_out, decoder_1_out3, and_1_out);
  Register #(.width(4), .trigger("falling")) register_1 (
    .D(Write_Data), .Q(register_1_q), .clk(and_2_out), .clr(not_2_out));  // open: en
  Register #(.width(4), .trigger("falling")) register_2 (
    .D(Write_Data), .Q(register_2_q), .clk(and_3_out), .clr(not_2_out));  // open: en
  Register #(.width(4), .trigger("falling")) register_3 (
    .D(Write_Data), .Q(register_3_q), .clk(and_4_out), .clr(not_2_out));  // open: en
  Register #(.width(4), .trigger("falling")) register_4 (
    .D(Write_Data), .Q(register_4_q), .clk(and_5_out), .clr(not_2_out));  // open: en
  not not_2 (not_2_out, CLR);
  Multiplexer #(.select(2), .width(4), .enable("false")) multiplexer_1 (
    .in0(register_1_q), .in1(register_2_q), .in2(register_3_q), .in3(register_4_q), .out(Read_Data1),
    .sel(Rd1));
  Multiplexer #(.select(2), .width(4), .enable("false")) multiplexer_2 (
    .in0(register_1_q), .in1(register_2_q), .in2(register_3_q), .in3(register_4_q), .out(Read_Data2),
    .sel(Rd2));
endmodule

module _3_Bit_Ripple_Carry_Adder (
  input  Cin,
  input  A,
  input  B,
  input  A_2,
  input  B_2,
  input  A_3,
  input  B_3,
  output [2:0] Output,
  output Carry_Flag
);

  wire n1bit_fa_1_carry, n1bit_fa_2_carry;

  _1bit_FA u_1bit_fa_1 (.A(A), .B(B), .C(Cin), .Carry(n1bit_fa_1_carry), .Sum(Output[0]));
  _1bit_FA u_1bit_fa_2 (.A(A_2), .B(B_2), .C(n1bit_fa_1_carry), .Carry(n1bit_fa_2_carry), .Sum(Output[1]));
  _1bit_FA u_1bit_fa_3 (.A(A_3), .B(B_3), .C(n1bit_fa_2_carry), .Carry(Carry_Flag), .Sum(Output[2]));
endmodule

module Adder_Subtractor (
  input  in_1,
  input  in_2,
  input  in_3,
  output out_4,
  output out_5
);

  wire XOR_out;

  _1bit_FA u_1bit_fa_1 (.A(in_2), .B(XOR_out), .C(in_1), .Carry(out_5), .Sum(out_4));
  xor XOR (XOR_out, in_1, in_3);
endmodule

module Instruction_Memory (
  input  [3:0] Address,
  output [15:0] Instruction
);

  ROM #(.addrWidth(4), .dataWidth(16)) rom_1 (.addr(Address), .data(Instruction));  // open: sel

  // Notes on the sheet:
  //   contents of rom_1 (hex, n*v repeats v):
  //   601 f30 e90 651 f71 ed1 681 454 a9b c0a 260 c0c f32
endmodule

module Data_Memory (
  input  [3:0] Address,
  input  [3:0] Write_Data,
  input  MRD,
  input  MWR,
  input  CLK,
  input  CLR,
  output [3:0] Read_Data
);

  wire AND_out, not_1_out, not_2_out, not_3_out, OR_out;
  wire [3:0] ram_1_data;

  or OR (OR_out, MWR, CLK);
  not not_1 (not_1_out, MRD);
  and AND (AND_out, MWR, not_1_out);
  not not_2 (not_2_out, CLR);
  RAM #(.addrWidth(4), .dataWidth(4)) ram_1 (
    .addr(Address), .data(ram_1_data), .clk(OR_out), .ld(AND_out), .clr(not_2_out));  // open: sel
  not not_3 (not_3_out, AND_out);
  assign Read_Data = AND_out ? ram_1_data : 4'bz;  // Controlled_Buffer controlled_buffer_1
  assign ram_1_data = not_3_out ? Write_Data : 4'bz;  // Controlled_Buffer controlled_buffer_2
endmodule

module Program_Counter (
  input  CLK,
  input  CLR,
  output [3:0] PCNew
);

  wire not_1_out;
  wire [3:0] adder_1_out;

  Register #(.width(4)) register_1 (.D(adder_1_out), .Q(PCNew), .clk(CLK), .clr(not_1_out));  // open: en
  not not_1 (not_1_out, CLR);
  Adder #(.width(4)) adder_1 (.a(4'b0001), .b(PCNew), .out(adder_1_out));  // open: cin, cout
endmodule

module Control_Unit (
  input  [3:0] in,
  output [15:0] out
);

  ROM #(.addrWidth(4), .dataWidth(16)) rom_1 (.addr(in), .data(out));  // open: sel

  // Notes on the sheet:
  //   contents of rom_1 (hex, n*v repeats v):
  //   79 479 879 b79 6d 46d 86d b6d f79 f6d be3 be3 e0 1 825 8cd
endmodule

module Processor (
  input  CLR,
  output [15:0] out_2
);

  wire and_1_out, CLK_out, n4_bit_alu_1_zf, not_1_out, or_1_out;
  wire [1:0] multiplexer_1_out;
  wire [3:0] adder_1_out, adder_2_out, data_memory_1_read_data, multiplexer_2_out, multiplexer_3_out,
       multiplexer_4_out, multiplexer_5_out, n4_bit_alu_1_out_6, register_1_q, register_file_1_read_data1,
       register_file_1_read_data2;
  wire [15:0] control_unit_1_out;

  Register #(.width(4)) register_1 (
    .D(multiplexer_4_out), .Q(register_1_q), .clk(CLK_out), .clr(not_1_out));  // open: en
  Clock CLK (.out(CLK_out));
  not not_1 (not_1_out, CLR);
  Adder #(.width(4)) adder_1 (.a(register_1_q), .b(4'b0001), .out(adder_1_out));  // open: cin, cout
  Instruction_Memory instruction_memory_1 (.Address(register_1_q), .Instruction(out_2));
  Multiplexer #(.width(2), .enable("false")) multiplexer_1 (
    .in0(out_2[5:4]), .in1(out_2[3:2]), .out(multiplexer_1_out), .sel(control_unit_1_out[4]));
  or or_1 (or_1_out, control_unit_1_out[7], CLK_out);
  Register_File register_file_1 (
    .Write_Address(multiplexer_1_out), .Write_Data(multiplexer_5_out),
    .Read_Data2(register_file_1_read_data2), .Rd0___Wr1(or_1_out), .CLR(CLR),
    .Read_Data1(register_file_1_read_data1), .Rd1(out_2[7:6]), .Rd2(out_2[5:4]), .Clock(CLK_out));
  Control_Unit control_unit_1 (.in(out_2[11:8]), .out(control_unit_1_out));
  Multiplexer #(.width(4), .enable("false")) multiplexer_2 (
    .in0(register_file_1_read_data2), .in1(out_2[3:0]), .out(multiplexer_2_out), .sel(control_unit_1_out[2]));
  Adder #(.width(4)) adder_2 (.a(adder_1_out), .b(out_2[3:0]), .out(adder_2_out));  // open: cin, cout
  _4_Bit_ALU u_4_bit_alu_1 (
    .in_3(register_file_1_read_data1), .in_4(multiplexer_2_out), .out_6(n4_bit_alu_1_out_6),
    .ZF(n4_bit_alu_1_zf), .Add0_Sub1(control_unit_1_out[9]), .Cin(control_unit_1_out[8]),
    .ALUop(control_unit_1_out[11:10]));  // open: SF, OF, CF
  and and_1 (and_1_out, control_unit_1_out[1], n4_bit_alu_1_zf);
  Multiplexer #(.width(4), .enable("false")) multiplexer_3 (
    .in0(adder_1_out), .in1(adder_2_out), .out(multiplexer_3_out), .sel(and_1_out));
  Data_Memory data_memory_1 (
    .Address(n4_bit_alu_1_out_6), .Write_Data(register_file_1_read_data2),
    .Read_Data(data_memory_1_read_data), .MRD(control_unit_1_out[6]), .MWR(control_unit_1_out[5]),
    .CLK(CLK_out), .CLR(CLR));
  Multiplexer #(.width(4), .enable("false")) multiplexer_4 (
    .in0(out_2[3:0]), .in1(multiplexer_3_out), .out(multiplexer_4_out), .sel(control_unit_1_out[0]));
  Multiplexer #(.width(4), .enable("false")) multiplexer_5 (
    .in0(data_memory_1_read_data), .in1(n4_bit_alu_1_out_6), .out(multiplexer_5_out),
    .sel(control_unit_1_out[3]));

  // Notes on the sheet:
  //   RegDst
  //   ALUSrc
  //   Branch
  //   Jmp
  //   MemToReg
endmodule
